# Fritzing sketch Penny guitar (saved by Fritzing 0.9.3b)
circuit board: 8.46667cm x 5.64444cm
perfboards: 1

parts:
  R1 = Resistor [tolerance=±5% resistance=220 package=THT]
  R2 = Resistor [tolerance=±5% resistance=220 package=THT]
  R3 = Resistor [tolerance=±5% resistance=330 package=THT]
  R4 = Resistor [tolerance=±5% resistance=330 package=THT]
  R5 = Resistor [tolerance=±5% resistance=330 package=THT]
  R6 = Resistor [tolerance=±5% resistance=330 package=THT]
  R7 = Resistor [tolerance=±5% resistance=220 package=THT]
  J1 = male pin header, 4 pins [form="♂ (male)"]
  J2 = male pin header, 10 pins [form="♂ (male)"]
  J3 = male pin header, 10 pins [form="♂ (male)"]
  LED1 = LED - 3mm [color="Green (570nm)" package="3 mm [THT]"]
  R8 = Resistor [tolerance=±5% resistance=100 package=THT]
  Part1 = Arduino Uno (Rev3)
  LED2 = LED - 5mm [color="Red (633nm)" package="5 mm [THT]"]
  LED4 = LED - 5mm [color="Red (633nm)" package="5 mm [THT]"]
  LED5 = LED - 5mm [color="Red (633nm)" package="5 mm [THT]"]
  LED6 = LED - 5mm [color="Red (633nm)" package="5 mm [THT]"]
  LED7 = LED - 5mm [color="Red (633nm)" package="5 mm [THT]"]
  LED8 = LED - 5mm [color="Red (633nm)" package="5 mm [THT]"]
  LED9 = LED - 5mm [color="Red (633nm)" package="5 mm [THT]"]
  LED10 = LED - 5mm [color="Red (633nm)" package="5 mm [THT]"]
  LED11 = LED - 5mm [color="Red (633nm)" package="5 mm [THT]"]
  LED12 = LED - 5mm [color="Red (633nm)" package="5 mm [THT]"]
  LED13 = LED - 5mm [color="Red (633nm)" package="5 mm [THT]"]
  LED14 = LED - 5mm [color="Red (633nm)" package="5 mm [THT]"]
  DIN1 = DIN-5 jack (MIDI) [package=THT]

nets:
  N1: R1.Pin_0, J1.pin4, DIN1.4
  N2: R1.Pin_1, J2.pin3, Part1.D1/TX
  N3: R2.Pin_0, J1.pin1, DIN1.5
  N4: R2.Pin_1, R7.Pin_1, J2.pin1, Part1.5V
  N5: R3.Pin_0, LED2.anode, LED4.cathode, LED9.anode, LED10.cathode, LED13.anode, LED14.cathode
  N6: R3.Pin_1, J3.pin1, Part1.D9_PWM
  N7: R4.Pin_0, LED2.cathode, LED4.anode, LED5.anode, LED6.cathode, LED11.anode, LED12.cathode
  N8: R4.Pin_1, J3.pin2, Part1.D10_PWM/SS
  N9: R5.Pin_0, LED5.cathode, LED6.anode, LED7.anode, LED8.cathode, LED9.cathode, LED10.anode
  N10: R5.Pin_1, J3.pin3, Part1.D11_PWM/MOSI
  N11: R6.Pin_0, LED7.cathode, LED8.anode, LED11.cathode, LED12.anode, LED13.cathode, LED14.anode
  N12: R6.Pin_1, J3.pin4, Part1.D12/MISO
  N13: R7.Pin_0, LED1.anode
  N14: J1.pin3, J2.pin2, R8.Pin_0, Part1.GND, DIN1.2
  N15: J2.pin4, Part1.D6_PWM
  N16: LED1.cathode, R8.Pin_1
